# Fritzing sketch killswitch (saved by Fritzing 0.9.3b)
perfboards: 1

parts:
  Raspberry_Pi_1 = Raspberry Pi 3 [part_number=RPI-3-V1.2]
  S1 = Round Pushbutton
  R1 = Resistor [tolerance=±5% resistance=220 package="2512 [SMD]"]
  LED1 = RGB LED (com. cathode, rgb) [package="5 mm [THT]"]
  J1 = female pin header, 10 pins [form="♀ (female)"]
  J2 = female pin header, 10 pins [form="♀ (female)"]
  J3 = female pin header, 6 pins [form="♀ (female)"]
  R2 = Resistor [tolerance=±5% resistance=220 package="2512 [SMD]"]

nets:
  N1: Raspberry_Pi_1.3v3, R1.Pin_0
  N2: Raspberry_Pi_1.GND, LED1.common_cathode
  N3: Raspberry_Pi_1.GIPO17, LED1.red_anode
  N4: Raspberry_Pi_1.GIPO27, LED1.green_anode
  N5: Raspberry_Pi_1.GIPO22, LED1.blue_anode
  N6: Raspberry_Pi_1.GIPO15, S1.leg1
  N7: S1.leg0, R1.Pin_1
  N8: J1.pin1, R2.Pin_0
  N9: J1.pin5, J3.pin3
  N10: J1.pin6, J3.pin4
  N11: J1.pin7, J3.pin5
  N12: J1.pin8, J3.pin6
  N13: J2.pin5, J3.pin2
  N14: J3.pin1, R2.Pin_1

notes:
  3V GPIO - B G R
